// Logisim project ALU.circ as structural Verilog: 1 circuit, main circuit ALU
module ALU (
  input  [31:0] A,
  input  [31:0] B,
  input  [4:0] Shift,
  input  CarryIn,
  input  [3:0] Codop,
  output [31:0] S,
  output [3:0] Flags
);

  wire and_4_out, and_5_out, and_6_out, and_7_out, and_8_out, and_9_out, and_10_out, and_11_out, and_12_out,
       and_13_out, and_14_out, and_15_out, bitselector_2_out, bitselector_3_out, bitselector_4_out,
       bitselector_5_out, bitselector_6_out, bitselector_7_out, comparator_2_eq, comparator_3_eq,
       comparator_4_eq, comparator_4_lt, comparator_5_eq, comparator_5_lt, comparator_6_eq, comparator_7_eq,
       comparator_8_eq, comparator_8_lt, comparator_9_eq, comparator_9_lt, comparator_10_gt,
       comparator_10_lt, negator_1_out, or_2_out, or_3_out, S1, S2, S3, S4, Signe;
  wire [4:0] subtractor_4_out, subtractor_5_out;
  wire [31:0] adder_1_out, adder_2_out, and_1_out, and_2_out, and_3_out, multiplier_1_out, not_1_out,
       not_2_out, or_1_out, shifter_1_out, shifter_2_out, shifter_3_out, shifter_4_out, subtractor_1_out,
       subtractor_2_out, subtractor_3_out, xor_1_out;

  Negator #(.width(1)) negator_1 (.in(CarryIn), .out(negator_1_out));
  assign not_1_out = ~B;  // NOT_Gate not_1, 32 bits wide
  assign not_2_out = ~B;  // NOT_Gate not_2, 32 bits wide
  assign and_1_out = A & B;  // AND_Gate and_1, 32 bits wide
  assign xor_1_out = A ^ B;  // XOR_Gate xor_1, 32 bits wide
  Shifter #(.width(32)) shifter_1 (.in(B), .\dist (Shift), .out(shifter_1_out));
  Shifter #(.shift("lr"), .width(32)) shifter_2 (.in(B), .\dist (Shift), .out(shifter_2_out));
  Shifter #(.shift("ar"), .width(32)) shifter_3 (.in(B), .\dist (Shift), .out(shifter_3_out));
  Adder #(.width(32)) adder_1 (.a(A), .b(B), .out(adder_1_out), .cin(CarryIn), .cout(S1));
  Subtractor #(.width(32)) subtractor_1 (.a(A), .b(B), .out(subtractor_1_out), .bin(negator_1_out), .bout(S2));
  Shifter #(.shift("rr"), .width(32)) shifter_4 (.in(B), .\dist (Shift), .out(shifter_4_out));
  assign and_2_out = A & B;  // AND_Gate and_2, 32 bits wide
  Subtractor #(.width(32)) subtractor_2 (.a({32{1'b0}}), .b(B), .out(subtractor_2_out));  // open: bin, bout
  Subtractor #(.width(32)) subtractor_3 (.a(A), .b(B), .out(subtractor_3_out), .bout(S3));  // open: bin
  Adder #(.width(32)) adder_2 (.a(A), .b(B), .out(adder_2_out), .cout(S4));  // open: cin
  assign or_1_out = A | B;  // OR_Gate or_1, 32 bits wide
  Multiplier #(.width(32)) multiplier_1 (.a(A), .b(B), .out(multiplier_1_out));  // open: cin, cout
  assign and_3_out = A & not_1_out;  // AND_Gate and_3, 32 bits wide
  Multiplexer #(.enable("false"), .select(4), .width(32)) multiplexer_1 (
    .in0(and_1_out), .in1(xor_1_out), .in2(shifter_1_out), .in3(shifter_2_out), .in4(shifter_3_out),
    .in5(adder_1_out), .in6(subtractor_1_out), .in7(shifter_4_out), .in8(and_2_out), .in9(subtractor_2_out),
    .in10(subtractor_3_out), .in11(adder_2_out), .in12(or_1_out), .in13(multiplier_1_out), .in14(and_3_out),
    .in15(not_2_out), .out(S), .sel(Codop));
  BitSelector #(.width(32)) bitselector_1 (.in(S), .out(Signe), .sel({5{1'b1}}));
  BitSelector #(.width(32)) bitselector_2 (.in(B), .out(bitselector_2_out), .sel(subtractor_4_out));
  Subtractor #(.width(5)) subtractor_4 (.a({5{1'b0}}), .b(Shift), .out(subtractor_4_out));  // open: bin, bout
  BitSelector #(.width(32)) bitselector_3 (.in(B), .out(bitselector_3_out), .sel(subtractor_5_out));
  Subtractor #(.width(5)) subtractor_5 (.a(Shift), .b({5{1'b0}}), .out(subtractor_5_out));  // open: bin, bout
  Comparator #(.width(32)) comparator_1 (.a(S), .b({32{1'b0}}), .eq(Flags[2]), .lt(Flags[3]));  // open: gt
  Multiplexer #(.enable("false"), .select(4)) multiplexer_2 (
    .in0(1'b0), .in1(1'b0), .in2(bitselector_2_out), .in3(bitselector_3_out), .in4(bitselector_3_out),
    .in5(S1), .in6(S2), .in7(1'b0), .in8(1'b0), .in9(1'b0), .in10(S3), .in11(S4), .in12(1'b0), .in13(1'b0),
    .in14(1'b0), .in15(1'b0), .out(Flags[1]), .sel(Codop));
  BitSelector #(.width(32)) bitselector_4 (.in(A), .out(bitselector_4_out), .sel({5{1'b1}}));
  BitSelector #(.width(32)) bitselector_5 (.in(B), .out(bitselector_5_out), .sel({5{1'b1}}));
  BitSelector #(.width(32)) bitselector_6 (.in(A), .out(bitselector_6_out), .sel({5{1'b1}}));
  BitSelector #(.width(32)) bitselector_7 (.in(B), .out(bitselector_7_out), .sel({5{1'b1}}));
  Comparator #(.width(4)) comparator_2 (.a(Codop), .b(4'b0101), .eq(comparator_2_eq));  // open: gt, lt
  Comparator #(.width(4)) comparator_3 (.a(Codop), .b(4'b1011), .eq(comparator_3_eq));  // open: gt, lt
  Comparator #(.width(1)) comparator_4 (
    .a(bitselector_4_out), .b(1'b0), .eq(comparator_4_eq), .lt(comparator_4_lt));  // open: gt
  Comparator #(.width(1)) comparator_5 (
    .a(bitselector_5_out), .b(1'b0), .eq(comparator_5_eq), .lt(comparator_5_lt));  // open: gt
  Comparator #(.width(4)) comparator_6 (.a(Codop), .b(4'b0110), .eq(comparator_6_eq));  // open: gt, lt
  Comparator #(.width(4)) comparator_7 (.a(Codop), .b(4'b1010), .eq(comparator_7_eq));  // open: gt, lt
  Comparator #(.width(1)) comparator_8 (
    .a(bitselector_6_out), .b(1'b0), .eq(comparator_8_eq), .lt(comparator_8_lt));  // open: gt
  Comparator #(.width(1)) comparator_9 (
    .a(bitselector_7_out), .b(1'b0), .eq(comparator_9_eq), .lt(comparator_9_lt));  // open: gt
  or or_2 (or_2_out, comparator_2_eq, comparator_3_eq);
  and and_4 (and_4_out, comparator_4_eq, comparator_5_eq);
  and and_5 (and_5_out, comparator_4_lt, comparator_5_lt);
  or or_3 (or_3_out, comparator_6_eq, comparator_7_eq);
  and and_6 (and_6_out, comparator_8_lt, comparator_9_eq);
  and and_7 (and_7_out, comparator_8_eq, comparator_9_lt);
  and and_8 (and_8_out, or_3_out, and_6_out);
  and and_9 (and_9_out, and_7_out, or_3_out);
  and and_10 (and_10_out, or_2_out, and_4_out);
  and and_11 (and_11_out, and_5_out, or_2_out);
  Comparator #(.width(1)) comparator_10 (
    .a(Signe), .b(1'b0), .gt(comparator_10_gt), .lt(comparator_10_lt));  // open: eq
  and and_12 (and_12_out, comparator_10_lt, and_10_out);
  and and_13 (and_13_out, and_11_out, comparator_10_gt);
  and and_14 (and_14_out, comparator_10_lt, and_8_out);
  and and_15 (and_15_out, and_9_out, comparator_10_gt);
  or or_4 (Flags[0], and_12_out, and_13_out, and_14_out, and_15_out);

  // Other names for the same wires on the sheet: Overflow = Flags[0]; CarryOut = Flags[1]

  // Notes on the sheet:
  //   Note: for ROR, C = N
  //   Note 2: assume that shift > 0 for LSL and LSR
endmodule
