// Logisim project Ctl_Conditional.circ as structural Verilog: 2 circuits, main circuit Conditional
module Conditional (
  input  Enable,
  input  [15:0] Instruction,
  input  N,
  input  Z,
  input  C,
  input  V,
  output [3:0] out_7,
  output [10:0] Offset,
  output out_9,
  output [7:0] out_10,
  output [10:0] out_11,
  output Verified
);

  wire flagcondition_1_s;
  wire [10:0] bit_extender_1_out;

  assign bit_extender_1_out = {{3{Instruction[7]}}, Instruction[7:0]};  // Bit_Extender bit_extender_1
  flagcondition flagcondition_1 (
    .bit11(Instruction[11]), .bit10(Instruction[10]), .bit09(Instruction[9]), .bit08(Instruction[8]), .N(N),
    .Z(Z), .C(C), .V(V), .s(flagcondition_1_s));
  Multiplexer #(.enable("false"), .width(11)) multiplexer_1 (
    .in0(bit_extender_1_out), .in1(Instruction[10:0]), .out(Offset), .sel(Instruction[13]));
  and and_1 (Verified, flagcondition_1_s, Enable);

  assign out_7 = Instruction[11:8];
  assign out_9 = Instruction[13];
  assign out_10 = Instruction[7:0];
  assign out_11 = Instruction[10:0];

  // Other names for the same wires on the sheet: EN = Enable; imm8[7:0] = Instruction[7:0];
  //   imm11[10:0] = Instruction[10:0]; cond[3:0] = Instruction[11:8]; B = Instruction[13]
endmodule

module flagcondition (
  input  bit11,
  input  bit10,
  input  bit09,
  input  bit08,
  input  N,
  input  Z,
  input  C,
  input  V,
  output s
);

  wire and_1_out, and_2_out, and_3_out, and_4_out, and_5_out, and_6_out, and_7_out, and_8_out, and_9_out,
       and_10_out, and_11_out, and_12_out, and_13_out, and_14_out, and_15_out, and_16_out, and_17_out,
       and_18_out, and_19_out, and_20_out, not_1_out, not_2_out, not_3_out, not_4_out, not_5_out, not_6_out,
       not_7_out, not_8_out;

  not not_1 (not_1_out, bit11);
  not not_2 (not_2_out, bit10);
  not not_3 (not_3_out, bit09);
  not not_4 (not_4_out, bit08);
  not not_5 (not_5_out, N);
  not not_6 (not_6_out, Z);
  not not_7 (not_7_out, C);
  not not_8 (not_8_out, V);
  and and_1 (and_1_out, not_1_out, not_2_out, not_3_out, not_4_out, Z);
  and and_2 (and_2_out, not_1_out, not_2_out, not_3_out, bit08, not_6_out);
  and and_3 (and_3_out, not_2_out, not_3_out, bit08, not_6_out, not_7_out);
  and and_4 (and_4_out, not_1_out, not_2_out, bit09, not_4_out, C);
  and and_5 (and_5_out, not_1_out, not_2_out, bit09, bit08, not_7_out);
  and and_6 (and_6_out, not_1_out, bit10, not_3_out, not_4_out, N);
  and and_7 (and_7_out, bit10, not_4_out, N, not_6_out, V);
  and and_8 (and_8_out, not_1_out, bit10, not_3_out, bit08, not_5_out);
  and and_9 (and_9_out, bit10, not_3_out, bit08, not_5_out, V);
  and and_10 (and_10_out, bit10, bit09, not_4_out, V);
  and and_11 (and_11_out, not_1_out, bit10, bit09, bit08, not_8_out);
  and and_12 (and_12_out, bit11, not_2_out, not_3_out, not_4_out, not_6_out, C);
  and and_13 (and_13_out, bit11, not_3_out, bit08, Z);
  and and_14 (and_14_out, bit11, bit09, not_4_out, not_5_out, not_8_out);
  and and_15 (and_15_out, bit11, bit09, not_4_out, N, V);
  and and_16 (and_16_out, bit11, not_2_out, bit09, bit08, not_5_out, V);
  and and_17 (and_17_out, bit11, not_2_out, bit09, bit08, N, not_8_out);
  and and_18 (and_18_out, bit11, bit10, not_4_out, not_5_out, not_6_out, not_8_out);
  and and_19 (and_19_out, bit11, bit10, not_3_out, bit08, N, not_8_out);
  and and_20 (and_20_out, bit11, bit10, bit09, not_4_out);
  or or_1 (s, and_1_out, and_2_out, and_3_out, and_4_out, and_5_out, and_6_out, and_7_out, and_8_out, and_9_out, and_10_out, and_11_out, and_12_out, and_13_out, and_14_out, and_15_out, and_16_out, and_17_out, and_18_out, and_19_out, and_20_out);
endmodule
