// Logisim project Ctl_Data_Processing.circ as structural Verilog: 2 circuits, main circuit Data_Processing
module Flags_Update (
  input  e0,
  input  e1,
  input  e2,
  input  e3,
  output N,
  output Z,
  output C,
  output V
);

  wire and_1_out, and_2_out, and_3_out, and_4_out, and_5_out, not_1_out, not_2_out, not_3_out, not_4_out;

  not not_1 (not_1_out, e0);
  not not_2 (not_2_out, e1);
  not not_3 (not_3_out, e2);
  not not_4 (not_4_out, e3);
  and and_1 (and_1_out, not_2_out, e2);
  and and_2 (and_2_out, not_1_out, e1);
  and and_3 (and_3_out, not_1_out, e1, not_3_out, e3);
  and and_4 (and_4_out, not_1_out, e1, e2, not_4_out);
  and and_5 (and_5_out, e0, not_2_out, e2);
  or or_1 (C, and_1_out, and_2_out);
  or or_2 (V, and_3_out, and_4_out, and_5_out);

  assign N = 1'b1;
  assign Z = 1'b1;
endmodule

module Data_Processing (
  input  Enable,
  input  [15:0] Instruction,
  output [2:0] Rd,
  output [2:0] Rn,
  output [2:0] Rm,
  output [3:0] ALU_Opcode,
  output [3:0] Flags_Update_Mask
);

  wire [3:0] flags_update_1_n;

  Multiplexer #(.enable("false"), .width(3)) multiplexer_1 (
    .in0(3'b000), .in1(Instruction[2:0]), .out(Rd), .sel(Enable));
  Multiplexer #(.enable("false"), .width(3)) multiplexer_2 (
    .in0(3'b000), .in1(Instruction[5:3]), .out(Rm), .sel(Enable));
  Multiplexer #(.enable("false"), .width(4)) multiplexer_3 (
    .in0(4'b0000), .in1(Instruction[9:6]), .out(ALU_Opcode), .sel(Enable));
  Flags_Update flags_update_1 (
    .e0(Instruction[6]), .e1(Instruction[7]), .e2(Instruction[8]), .e3(Instruction[9]),
    .N(flags_update_1_n[0]), .Z(flags_update_1_n[1]), .C(flags_update_1_n[2]), .V(flags_update_1_n[3]));
  Multiplexer #(.enable("false"), .width(4)) multiplexer_4 (
    .in0(4'b0000), .in1(flags_update_1_n), .out(Flags_Update_Mask), .sel(Enable));

  assign Rn = Rd;

  // Notes on the sheet:
  //   Pull output low on Enable = 0
endmodule
