// Logisim project Ctl_Flags_APSR.circ as structural Verilog: 1 circuit, main circuit Flags_APSR
module Flags_APSR (
  input  [3:0] Update_Mask,
  input  [3:0] Flags_In,
  input  Clk,
  input  Rst,
  output [3:0] Flags_Out
);

  Register #(.width(1)) register_1 (.D(Update_Mask[2]), .en(Flags_In[2]), .clk(Clk), .Q(Flags_Out[2]), .clr(Rst));
  Register #(.width(1)) register_2 (.D(Update_Mask[1]), .en(Flags_In[1]), .clk(Clk), .Q(Flags_Out[1]), .clr(Rst));
  Register #(.width(1)) register_3 (.D(Update_Mask[0]), .en(Flags_In[0]), .clk(Clk), .Q(Flags_Out[0]), .clr(Rst));
  Register #(.width(1)) register_4 (.D(Update_Mask[3]), .en(Flags_In[3]), .clk(Clk), .Q(Flags_Out[3]), .clr(Rst));

  // Other names for the same wires on the sheet: I_V = Flags_In[0]; I_C = Flags_In[1]; I_Z = Flags_In[2];
  //   I_N = Flags_In[3]; S_V = Flags_Out[0]; S_C = Flags_Out[1]; S_Z = Flags_Out[2]; S_N = Flags_Out[3];
  //   U_V = Update_Mask[0]; U_C = Update_Mask[1]; U_Z = Update_Mask[2]; U_N = Update_Mask[3]
endmodule
