// Logisim project Ctl_Shift_Add_Sub_Mov.circ as structural Verilog: 3 circuits, main circuit Shift_Add_Sub_Mov
module Shift_Add_Sub_Mov (
  input  [15:0] Instruction,
  input  Enable,
  output [3:0] Flags_Update_Mask,
  output Carry,
  output Imm32_Enable,
  output [2:0] Rm,
  output [2:0] Rn,
  output [2:0] Rd,
  output [7:0] Imm8,
  output [4:0] Imm5,
  output [2:0] Imm3,
  output [31:0] Imm32,
  output [3:0] ALU_Opcode,
  output [31:0] out_14
);

  wire ADD_3i, ADD_8i, ADD_R, ASR, CMP, Imm3_EN, Imm8_EN, Imm32_EN, LSL, LSR, MOV, not_1_out, not_2_out,
       not_3_out, not_4_out, not_5_out, not_6_out, not_7_out, not_8_out, not_9_out, not_10_out, not_11_out,
       not_12_out, not_13_out, not_14_out, not_15_out, not_16_out, not_17_out, not_18_out, not_19_out, Rm_EN,
       Rn_EN, SHIFT, SUB, SUB_3i, SUB_8i, SUB_R;
  wire [2:0] multiplexer_2_out, Rd_t, Rm_t, Rn_t;
  wire [3:0] ALUOP, FUM;
  wire [4:0] Imm5_t;
  wire [7:0] negator_1_out;
  wire [31:0] bit_extender_1_out, bit_extender_2_out, Imm32_t, multiplexer_6_out;

  Negator negator_1 (.in(Instruction[7:0]), .out(negator_1_out));
  Multiplexer #(.enable("false"), .width(8)) multiplexer_1 (
    .in0(Instruction[7:0]), .in1(negator_1_out), .out(Imm8), .sel(MOV));
  Multiplexer #(.enable("false"), .width(3)) multiplexer_2 (
    .in0(Instruction[8:6]), .in1(Instruction[5:3]), .out(multiplexer_2_out), .sel(SHIFT));
  Multiplexer #(.enable("false"), .width(3)) multiplexer_3 (
    .in0(3'b000), .in1(Instruction[5:3]), .out(Rn_t), .sel(Rn_EN));
  Multiplexer #(.enable("false"), .width(3)) multiplexer_4 (
    .in0(Instruction[2:0]), .in1(Instruction[10:8]), .out(Rd_t), .sel(Imm8_EN));
  Multiplexer #(.enable("false"), .width(5)) multiplexer_5 (
    .in0({5{1'b0}}), .in1(Instruction[10:6]), .out(Imm5_t), .sel(SHIFT));
  assign bit_extender_1_out = {{29{1'b0}}, Instruction[8:6]};  // Bit_Extender bit_extender_1
  assign bit_extender_2_out = {{24{1'b0}}, Imm8};  // Bit_Extender bit_extender_2
  Multiplexer #(.enable("false"), .width(32)) multiplexer_6 (
    .in0(bit_extender_1_out), .in1(bit_extender_2_out), .out(multiplexer_6_out), .sel(Imm8_EN));
  Multiplexer #(.enable("false"), .width(3)) multiplexer_7 (
    .in0(3'b000), .in1(multiplexer_2_out), .out(Rm_t), .sel(Rm_EN));
  Multiplexer #(.enable("false"), .width(32)) multiplexer_8 (
    .in0({32{1'b0}}), .in1(multiplexer_6_out), .out(Imm32_t), .sel(Imm32_EN));
  or or_1 (SHIFT, LSL, LSR, ASR);
  or or_2 (Imm3_EN, ADD_3i, SUB_3i);
  or or_3 (Imm8_EN, ADD_8i, SUB_8i, MOV, CMP);
  or or_4 (Rn_EN, ADD_R, SUB_R, ADD_3i, SUB_3i);
  or or_5 (Imm32_EN, Imm3_EN, Imm8_EN);
  or or_6 (Rm_EN, SHIFT, ADD_R, SUB_R);
  or or_7 (SUB, SUB_R, SUB_3i, SUB_8i);
  not not_1 (not_1_out, Instruction[11]);
  not not_2 (not_2_out, Instruction[12]);
  not not_3 (not_3_out, Instruction[13]);
  not not_4 (not_4_out, Instruction[12]);
  not not_5 (not_5_out, Instruction[13]);
  not not_6 (not_6_out, Instruction[11]);
  not not_7 (not_7_out, Instruction[13]);
  not not_8 (not_8_out, Instruction[9]);
  not not_9 (not_9_out, Instruction[10]);
  not not_10 (not_10_out, Instruction[13]);
  not not_11 (not_11_out, Instruction[10]);
  not not_12 (not_12_out, Instruction[13]);
  not not_13 (not_13_out, Instruction[9]);
  not not_14 (not_14_out, Instruction[13]);
  not not_15 (not_15_out, Instruction[13]);
  not not_16 (not_16_out, Instruction[11]);
  not not_17 (not_17_out, Instruction[12]);
  not not_18 (not_18_out, Instruction[12]);
  not not_19 (not_19_out, Instruction[11]);
  and and_1 (LSL, not_1_out, not_2_out, not_3_out);
  and and_2 (LSR, Instruction[11], not_4_out, not_5_out);
  and and_3 (ASR, not_6_out, Instruction[12], not_7_out);
  and and_4 (ADD_R, not_8_out, not_9_out, Instruction[11], Instruction[12], not_10_out);
  and and_5 (SUB_R, Instruction[9], not_11_out, Instruction[11], Instruction[12], not_12_out);
  and and_6 (ADD_3i, not_13_out, Instruction[10], Instruction[11], Instruction[12], not_14_out);
  and and_7 (SUB_3i, Instruction[9], Instruction[10], Instruction[11], Instruction[12], not_15_out);
  and and_8 (MOV, not_16_out, not_17_out, Instruction[13]);
  and and_9 (CMP, Instruction[11], not_18_out, Instruction[13]);
  and and_10 (ADD_8i, not_19_out, Instruction[12], Instruction[13]);
  and and_11 (SUB_8i, Instruction[11], Instruction[12], Instruction[13]);
  Multiplexer #(.enable("false"), .width(3)) multiplexer_9 (.in0(3'b000), .in1(Rd_t), .out(Rd), .sel(Enable));
  Multiplexer #(.enable("false"), .width(4)) multiplexer_10 (
    .in0(4'b0000), .in1(FUM), .out(Flags_Update_Mask), .sel(Enable));
  and and_12 (Carry, SUB, Enable);
  and and_13 (Imm32_Enable, Imm32_EN, Enable);
  Multiplexer #(.enable("false"), .width(3)) multiplexer_11 (.in0(3'b000), .in1(Rm_t), .out(Rm), .sel(Enable));
  Multiplexer #(.enable("false"), .width(3)) multiplexer_12 (.in0(3'b000), .in1(Rn_t), .out(Rn), .sel(Enable));
  Multiplexer #(.enable("false"), .width(5)) multiplexer_13 (.in0({5{1'b0}}), .in1(Imm5_t), .out(Imm5), .sel(Enable));
  Multiplexer #(.enable("false"), .width(32)) multiplexer_14 (
    .in0({32{1'b0}}), .in1(Imm32_t), .out(Imm32), .sel(Enable));
  Multiplexer #(.enable("false"), .width(4)) multiplexer_15 (
    .in0(4'b0000), .in1(ALUOP), .out(ALU_Opcode), .sel(Enable));
  ALU2OP alu2op_1 (
    .bit13(Instruction[13]), .bit12(Instruction[12]), .bit11(Instruction[11]), .bit10(Instruction[10]),
    .bit09(Instruction[9]), .op3(ALUOP[3]), .op2(ALUOP[2]), .op1(ALUOP[1]), .op0(ALUOP[0]));
  Flag_Update_Mask flag_update_mask_1 (
    .bit13(Instruction[13]), .bit12(Instruction[12]), .bit11(Instruction[11]), .bit10(Instruction[10]),
    .bit09(Instruction[9]), .N(FUM[3]), .Z(FUM[2]), .C(FUM[1]), .V(FUM[0]));

  assign Imm3 = Instruction[8:6];

  // Other names for the same wires on the sheet: bit03 = Instruction[3]; bit04 = Instruction[4];
  //   bit05 = Instruction[5]; bit00 = Instruction[0]; bit01 = Instruction[1]; bit02 = Instruction[2];
  //   bit06 = Instruction[6]; bit07 = Instruction[7]; bit08 = Instruction[8]; bit09 = Instruction[9];
  //   bit10 = Instruction[10]; EN = Enable; bit11 = Instruction[11]; bit12 = Instruction[12]; bit13 = Instruction[13];
  //   bit14 = Instruction[14]; bit15 = Instruction[15]

  // Notes on the sheet:
  //   Pull output low on Enable = 0
  //   Note 3: Imm32_Enable forces the use of the immediate for Rm register
  //   Note: ALU uses Rn register for shifts. Use Rn instead of Rm for shifts (immediate) here too
  //   Note 2: MOV uses RSB ALU opcode with Imm8 reversed so that it is copied to output register
  //   only ADD and SUB use Rm
  //   Enable carry for SUB since it is reversed in ALU
  //   ALU will use Imm32 instead of Rm
endmodule

module ALU2OP (
  input  bit13,
  input  bit12,
  input  bit11,
  input  bit10,
  input  bit09,
  output op3,
  output op2,
  output op1,
  output op0
);

  wire and_2_out, and_3_out, and_4_out, and_5_out, and_6_out, and_7_out, not_1_out, not_2_out, not_3_out,
       not_4_out;

  not not_1 (not_1_out, bit13);
  not not_2 (not_2_out, bit12);
  not not_3 (not_3_out, bit11);
  not not_4 (not_4_out, bit09);
  and and_1 (op3, bit13, not_2_out);
  and and_2 (and_2_out, not_1_out, not_2_out);
  and and_3 (and_3_out, bit11, bit09);
  and and_4 (and_4_out, bit13, bit11);
  and and_5 (and_5_out, not_1_out, not_2_out, bit11);
  and and_6 (and_6_out, not_1_out, bit11, not_4_out);
  and and_7 (and_7_out, bit13, not_3_out);
  or or_1 (op1, and_2_out, and_3_out, and_4_out);
  or or_2 (op0, and_5_out, and_6_out, and_7_out);

  assign op2 = bit12;
endmodule

module Flag_Update_Mask (
  input  bit13,
  input  bit12,
  input  bit11,
  input  bit10,
  input  bit09,
  output N,
  output Z,
  output C,
  output V
);

  wire and_1_out, and_2_out, and_3_out, not_1_out;

  not not_1 (not_1_out, bit13);
  or or_1 (C, not_1_out, bit11, bit12);
  and and_1 (and_1_out, bit12, bit11);
  and and_2 (and_2_out, bit13, bit11);
  or or_2 (V, and_1_out, and_2_out, and_3_out);
  and and_3 (and_3_out, bit13, bit12);

  assign N = 1'b1;
  assign Z = 1'b1;
endmodule
